# Fritzing sketch tracker_diagram (saved by Fritzing 0.9.2b)
breadboards: 1

parts:
  S1 = Pushbutton [package="[THT]"]
  S2 = Pushbutton [package="[THT]"]
  S3 = Pushbutton [package="[THT]"]
  S4 = Pushbutton [package="[THT]"]
  Part1 = Arduino Uno (Rev3)
  R1 = Resistor [tolerance=±5% resistance=220 package=THT]
  R2 = Resistor [tolerance=±5% resistance=220 package=THT]
  R3 = Resistor [tolerance=±5% resistance=100 package=THT]
  LED1 = RGB LED - (4 legs) [package="5 mm [THT]"]

nets:
  N1: S1.Pin_1, S1.Pin_2, S2.Pin_1, S2.Pin_2, S3.Pin_1, S3.Pin_2, S4.Pin_1, S4.Pin_2, Part1.GND
  N2: S1.Pin_3, S1.Pin_4, Part1.D2
  N3: S2.Pin_3, S2.Pin_4, Part1.D3_PWM
  N4: S3.Pin_3, S3.Pin_4, Part1.D4
  N5: S4.Pin_3, S4.Pin_4, Part1.D5_PWM
  N6: Part1.D8, R3.Pin_1
  N7: Part1.D9_PWM, R1.Pin_1
  N8: Part1.D10_PWM/SS, LED1.blue_cathode
  N9: Part1.3V3, R2.Pin_1
  N10: R1.Pin_0, LED1.green_cathode
  N11: R2.Pin_0, LED1.common_anode
  N12: R3.Pin_0, LED1.red_cathode
